# Fritzing sketch Smart_Closet_Setup (saved by Fritzing 0.9.2b)

parts:
  Raspberry_Pi_B_rev2 = Raspberry Pi B rev2
  Parte1 = RFID-RC522-v2

nets:
  3V3: Raspberry_Pi_B_rev2.3V3, Parte1.3.3V
  GND: Raspberry_Pi_B_rev2.GND, Parte1.GND
  N1: Raspberry_Pi_B_rev2.GPIO_10, Parte1.MOSI
  N2: Raspberry_Pi_B_rev2.GPIO_9, Parte1.MISO
  N3: Raspberry_Pi_B_rev2.GPIO_25, Parte1.RST
  N4: Raspberry_Pi_B_rev2.GPIO_11, Parte1.SCK
  N5: Raspberry_Pi_B_rev2.GPIO_8, Parte1.SDA

custom parts:
  RFID-RC522-v2: A simple China made RFID-RC522 Reader; do check the pin labels, as this is a MFRC522 based clone.
